# Fritzing sketch RainbrellaSchematic (saved by Fritzing 0.9.3b)
breadboards: 1

parts:
  part = Arduino Uno (Rev3)
  LED_Strip_1 = WS2812 RGB LED matrix 1x8
  LED_Strip_2 = WS2812 RGB LED matrix 1x8
  LED_Strip_3 = WS2812 RGB LED matrix 1x8
  LED_Strip_4 = WS2812 RGB LED matrix 1x8
  Photoresistor = Photocell (LDR) [package=THT]
  Resistor = Resistor [tolerance=±5% resistance=10k package=THT]
  Relay = RELAY [package=relay-jzc]
  Reed_Switch = SWITCH-MOMENTARY-2 [package=reed_switch_pth]
  Temperature_and_Humidity_Sensor = mystery part, 4 pins [chip_label=DHT11]
  12v_Water_Pump = DC Motor
  part_2 = Rectifier Diode [package="300 mil [THT]"]

nets:
  N1: part.A0, Photoresistor.pin_0
  N2: part.D8, LED_Strip_1.DIN
  N3: part.D2, Temperature_and_Humidity_Sensor.pin2
  N4: part.D4, Reed_Switch.1
  N5: part.D7, Relay.COIL1
  GND: LED_Strip_1.GND#0, Resistor.Pin_1, Relay.COIL2, Reed_Switch.2, Temperature_and_Humidity_Sensor.pin4, 12v_Water_Pump.pin_2
  5V: LED_Strip_1.VCC#1
  N6: LED_Strip_1.VCC#5, LED_Strip_2.VCC#1
  N7: LED_Strip_1.DOUT, LED_Strip_2.DIN
  N8: LED_Strip_1.GND#7, LED_Strip_2.GND#0
  N9: LED_Strip_2.GND#4, LED_Strip_2.GND#7, LED_Strip_3.GND#0, LED_Strip_3.GND#3
  N10: LED_Strip_2.VCC#5, LED_Strip_3.VCC#1
  N11: LED_Strip_2.DOUT, LED_Strip_3.DIN
  N12: LED_Strip_3.GND#4, LED_Strip_3.GND#7, LED_Strip_4.GND
  N13: LED_Strip_3.VCC#5, LED_Strip_4.VCC
  N14: LED_Strip_3.DOUT, LED_Strip_4.DIN
  N15: Photoresistor.pin_1, Resistor.Pin_0
  N16: Relay.NO, 12v_Water_Pump.pin_1, part_2.anode
  12V: Relay.MAIN, part_2.cathode
  3.3V: Temperature_and_Humidity_Sensor.pin1

custom parts:
  WS2812 RGB LED matrix 1x8: WS2812 matrix 1x8
